# Fritzing sketch ahmed pcb (saved by Fritzing 0.9.3b)
breadboards: 2

parts:
  Raspberry_Pi_1 = Raspberry Pi 3 [part_number=RPI-3-V1.2]
  hc-sr1 = hc-sr04
  R1 = Resistor [tolerance=±5% resistance=220 package="0402 [SMD]"]
  R2 = Resistor [tolerance=±5% resistance=220 package="2512 [SMD]"]
  RHT1 = Humidity and Temperature Sensor RHT03
  Part2 = Photon
  LED2 = LED - 3mm [color="Red (633nm)" package="3 mm [THT]"]
  LED4 = LED - 3mm [color="Red (633nm)" package="3 mm [THT]"]
  LED5 = LED - 3mm [color="Red (633nm)" package="3 mm [THT]"]

nets:
  N1: Raspberry_Pi_1.GPIO4, LED5.anode
  N2: Raspberry_Pi_1.GPIO17, LED4.anode
  N3: Raspberry_Pi_1.GPIO27, RHT1.Data-signal
  N4: Raspberry_Pi_1.GPIO25, R1.Pin_1, R2.Pin_0
  N5: Raspberry_Pi_1.GPIO23, hc-sr1.Trig
  GND: Raspberry_Pi_1.GND, hc-sr1.GND, R2.Pin_1, RHT1.GND_2, LED4.cathode
  VCC: Raspberry_Pi_1.5V, hc-sr1.VCC, RHT1.Vcc
  N6: hc-sr1.Echo, R1.Pin_0
  N7: Part2.GND, LED2.cathode
  N8: Part2.D4, LED2.anode
